# Fritzing sketch LEDTestBoard (saved by Fritzing 1.0.1rc)
circuit board: 8cm x 2cm
breadboards: 1

parts:
  V+ = female pin header, 2 pins [form="♀ (female)"]
  V+G = female pin header, 2 pins [form="♀ (female)"]
  V+B = female pin header, 2 pins [form="♀ (female)"]
  V+Y = female pin header, 2 pins [form="♀ (female)"]
  V+R = female pin header, 2 pins [form="♀ (female)"]
  GND = female pin header, 2 pins [form="♀ (female)"]
  G-G = female pin header, 2 pins [form="♀ (female)"]
  G-Y = female pin header, 2 pins [form="♀ (female)"]
  G-R = female pin header, 2 pins [form="♀ (female)"]
  G-B = female pin header, 2 pins [form="♀ (female)"]
  LEDG = LED - 5mm [color="Red (633nm)" current=0.030A package="5 mm [THT]"]
  LEDY = LED - 5mm [color="Red (633nm)" current=0.030A package="5 mm [THT]"]
  LEDR = LED - 5mm [color="Red (633nm)" current=0.030A package="5 mm [THT]"]
  LEDB = LED - 5mm [color="Red (633nm)" current=0.030A package="5 mm [THT]"]
  RG = Resistor [tolerance=±5% power=0.25W resistance=330 package=THT]
  RY = Resistor [tolerance=±5% power=0.25W resistance=330 package=THT]
  RR = Resistor [tolerance=±5% power=0.25W resistance=330 package=THT]
  RB = Resistor [tolerance=±5% power=0.25W resistance=330 package=THT]

nets:
  N1: V+.pin1, V+.pin2
  N2: V+G.pin1, V+G.pin2, LEDG.anode
  N3: V+B.pin1, V+B.pin2, LEDB.anode
  N4: V+Y.pin1, V+Y.pin2, LEDY.anode
  N5: V+R.pin1, V+R.pin2, LEDR.anode
  N6: GND.pin1, GND.pin2
  N7: G-G.pin1, G-G.pin2, RG.Pin_1
  N8: G-Y.pin1, G-Y.pin2, RY.Pin_1
  N9: G-R.pin1, G-R.pin2, RR.Pin_1
  N10: G-B.pin1, G-B.pin2, RB.Pin_1
  N11: LEDG.cathode, RG.Pin_0
  N12: LEDY.cathode, RY.Pin_0
  N13: LEDR.cathode, RR.Pin_0
  N14: LEDB.cathode, RB.Pin_0

notes:
  LED
  TestBoard
  V1.0  ©️2024
  ThatAintWorking
