# Fritzing sketch ServoDriver (saved by Fritzing 1.0.1rc)
circuit board: 7cm x 3cm
breadboards: 1

parts:
  ATtiny85 = attiny85 [package=dip]
  S2 = Pushbutton [package="[THT]"]
  S1 = Pushbutton [package="[THT]"]
  Servo = male pin header, 3 pins [form="♂ (male)"]
  R1 = Resistor [tolerance=±5% power=0.25W resistance=1k package=THT]
  I2C = male pin header, 4 pins [form="♂ (male)"]
  Power = male pin header, 2 pins [form="♂ (male)"]
  C1 = Ceramic Capacitor [capacitance=100nF voltage=35V package="100 mil [THT, multilayer]"]
  C2 = Ceramic Capacitor [capacitance=100nF voltage=35V package="100 mil [THT, multilayer]"]
  R2 = Resistor [tolerance=±5% power=0.25W resistance=4.7k package=THT]
  R3 = Resistor [tolerance=±5% power=0.25W resistance=4.7k package=THT]
  7805 = Voltage Regulator (flipped) [package=to-220-alt]

nets:
  N1: ATtiny85.Pin_1, R1.Pin_0
  N2: ATtiny85.Pin_2, S1.Pin_1, S1.Pin_2
  N3: ATtiny85.Pin_3, S2.Pin_3, S2.Pin_4
  N4: ATtiny85.Pin_4, S2.Pin_1, S2.Pin_2, S1.Pin_3, S1.Pin_4, Servo.pin1, I2C.pin1, Power.pin1, C1.0, C2.0, 7805.GND
  N5: ATtiny85.Pin_5, I2C.pin3, R3.Pin_1
  N6: ATtiny85.Pin_6, Servo.pin3
  N7: ATtiny85.Pin_7, I2C.pin4, R2.Pin_1
  N8: ATtiny85.Pin_8, Servo.pin2, R1.Pin_1, I2C.pin2, C1.1, R2.Pin_0, R3.Pin_0, 7805.OUT
  N9: Power.pin2, C2.1, 7805.IN

notes:
  GND
  VIN
  VCC
  PPM
  SCL
  SDA
  facedown
  with
  heatsink
  on top

custom parts:
  Voltage Regulator (flipped): Voltage Regulator Standard 7805 5V regulator. IGO (Input Ground Output). Spark Fun Electronics SKU : COM-00107
