# Fritzing sketch ServoDriver328P (saved by Fritzing 1.0.1rc)
circuit board: 7cm x 9cm
breadboards: 1

parts:
  100> = Pushbutton [package="[THT]"]
  <100 = Pushbutton [package="[THT]"]
  R1 = Resistor [tolerance=±5% power=0.25W resistance=330 package=THT]
  J3 = female pin header, 6 pins [form="♀ (female)"]
  J4 = female pin header, 6 pins [form="♀ (female)"]
  R2 = Resistor [tolerance=±5% power=0.25W resistance=330 package=THT]
  R3 = Resistor [tolerance=±5% power=0.25W resistance=220 package=THT]
  R4 = Resistor [tolerance=±5% power=0.25W resistance=330 package=THT]
  R5 = Resistor [tolerance=±5% power=0.25W resistance=330 package=THT]
  R6 = Resistor [tolerance=±5% power=0.25W resistance=220 package=THT]
  R7 = Resistor [tolerance=±5% power=0.25W resistance=330 package=THT]
  R8 = Resistor [tolerance=±5% power=0.25W resistance=330 package=THT]
  Servo = Dagu DGServo 9g header (male) [package=THT]
  C1 = Ceramic Capacitor [capacitance=100nF voltage=35V package="200 mil [THT, multilayer]"]
  ATmega328P = atmega328 [package=dip]
  Y1 = CRYSTAL [package=hc49u-v]
  7805 = Voltage Regulator [package=to-220-alt]
  C4 = Ceramic Capacitor [capacitance=100nF voltage=35V package="100 mil [THT, multilayer]"]
  C5 = Ceramic Capacitor [capacitance=100nF voltage=35V package="100 mil [THT, multilayer]"]
  C2 = Ceramic Capacitor [capacitance=100nF voltage=35V package="100 mil [THT, multilayer]"]
  C3 = Ceramic Capacitor [capacitance=100nF voltage=35V package="100 mil [THT, multilayer]"]
  S1 = SPST Switch [package=switch-spdt_kit]
  9V = Battery block 9V
  R9 = Resistor [tolerance=±5% power=0.25W resistance=22k package=THT]
  R10 = Resistor [tolerance=±5% power=0.25W resistance=1k package=THT]
  C7 = Ceramic Capacitor [capacitance=100nF voltage=35V package="100 mil [THT, multilayer]"]

nets:
  N1: 100>.Pin_1, 100>.Pin_2, ATmega328P.D10_(PWM)
  GND: 100>.Pin_3, 100>.Pin_4, <100.Pin_3, <100.Pin_4, Servo.gnd, C1.1, ATmega328P.GND, 7805.GND, C4.0, C5.1, C2.1, C3.0, 9V.-, R9.Pin_0, C7.1
  N2: <100.Pin_1, <100.Pin_2, ATmega328P.D9_(PWM)
  N3: R1.Pin_0, ATmega328P.D2
  N4: R1.Pin_1, J3.pin5
  N5: J3.pin1, R2.Pin_1
  N6: J3.pin2, ATmega328P.D12
  N7: J3.pin3, ATmega328P.D11_(PWM)
  N8: J3.pin4, R6.Pin_1
  N9: J3.pin6, ATmega328P.A4
  N10: J4.pin1, R5.Pin_1
  N11: J4.pin2, R4.Pin_1
  N12: J4.pin3, R8.Pin_1
  N13: J4.pin4, R3.Pin_1
  N14: J4.pin5, R7.Pin_1
  N15: J4.pin6, ATmega328P.D13
  N16: R2.Pin_0, ATmega328P.D3_(PWM)
  N17: R3.Pin_0, ATmega328P.D4
  N18: R4.Pin_0, ATmega328P.D5_(PWM)
  N19: R5.Pin_0, ATmega328P.D6_(PWM)
  N20: R6.Pin_0, ATmega328P.D7
  N21: R7.Pin_0, ATmega328P.D8
  N22: R8.Pin_0, ATmega328P.A5
  VCC: Servo.Vcc, C1.0, ATmega328P.VCC, ATmega328P.AVCC, ATmega328P.AREF, 7805.OUT, C4.1, C5.0, R10.Pin_1
  N23: Servo.pulse, ATmega328P.A0, R9.Pin_1
  N24: ATmega328P.RESET, R10.Pin_0
  N25: ATmega328P.XLAT1, Y1.1, C2.0
  N26: ATmega328P.XLAT2, Y1.2, C3.1
  N27: 7805.IN, S1.S, C7.0
  N28: S1.P, 9V.+

notes:
  1 A F 2 3 B
  E D * C G 4
  E
  D
  *
  C
  4
  G
  1
  A
  F
  2
  3
  B
  GND
  VCC
  PPM
  Servo Driver (328P)
  V1.0  ©2024 ThatAintWorking
  +
  -
  >
  <
