# Fritzing sketch ServoDriverNano (saved by Fritzing 1.0.1rc)
circuit board: 7cm x 9cm
breadboards: 1

parts:
  100> = Pushbutton [package="[THT]"]
  <100 = Pushbutton [package="[THT]"]
  Nano = Arduino Nano (Rev3.0)
  R1 = Resistor [tolerance=±5% power=0.25W resistance=220 package=THT]
  J3 = female pin header, 6 pins [form="♀ (female)"]
  J4 = female pin header, 6 pins [form="♀ (female)"]
  R2 = Resistor [tolerance=±5% power=0.25W resistance=220 package=THT]
  R3 = Resistor [tolerance=±5% power=0.25W resistance=220 package=THT]
  R4 = Resistor [tolerance=±5% power=0.25W resistance=220 package=THT]
  R5 = Resistor [tolerance=±5% power=0.25W resistance=220 package=THT]
  R6 = Resistor [tolerance=±5% power=0.25W resistance=220 package=THT]
  R7 = Resistor [tolerance=±5% power=0.25W resistance=220 package=THT]
  R8 = Resistor [tolerance=±5% power=0.25W resistance=220 package=THT]
  Servo = Dagu DGServo 9g header (male) [package=THT]
  C1 = Ceramic Capacitor [capacitance=100nF voltage=35V package="200 mil [THT, multilayer]"]

nets:
  GND: 100>.Pin_1, 100>.Pin_2, <100.Pin_1, <100.Pin_2, Nano.GND, Servo.gnd, C1.1
  N1: 100>.Pin_3, 100>.Pin_4, Nano.A1
  N2: <100.Pin_3, <100.Pin_4, Nano.A0
  N3: Nano.D2, R1.Pin_0
  N4: Nano.D3, R2.Pin_0
  N5: Nano.D4, R3.Pin_0
  N6: Nano.D5, R4.Pin_0
  N7: Nano.D6, R5.Pin_0
  N8: Nano.D7, R6.Pin_0
  N9: Nano.D8, R7.Pin_0
  N10: Nano.D9, R8.Pin_0
  N11: Nano.D10, J3.pin6
  N12: Nano.D11/MOSI, J3.pin3
  N13: Nano.D12/MISO, J3.pin2
  5V: Nano.5V, Servo.Vcc, C1.0
  N14: Nano.A7, Servo.pulse
  N15: Nano.D13/SCK, J4.pin6
  N16: R1.Pin_1, J3.pin5
  N17: J3.pin1, R2.Pin_1
  N18: J3.pin4, R6.Pin_1
  N19: J4.pin1, R5.Pin_1
  N20: J4.pin2, R4.Pin_1
  N21: J4.pin3, R8.Pin_1
  N22: J4.pin4, R3.Pin_1
  N23: J4.pin5, R7.Pin_1

notes:
  1 A F 2 3 B
  E D * C G 4
  E
  D
  *
  C
  4
  G
  1
  A
  F
  2
  3
  B
  GND
  VCC
  PPM
  Servo Driver (Nano)
  V1.0  ©2024 ThatAintWorking
