# Fritzing sketch ServoDriverShield (saved by Fritzing 1.0.1rc)
circuit board: 7cm x 5cm
breadboards: 1

parts:
  R1 = Resistor [tolerance=±5% power=0.25W resistance=220 package=THT]
  J1 = female pin header, 6 pins [form="♀ (female)"]
  J2 = female pin header, 6 pins [form="♀ (female)"]
  R2 = Resistor [tolerance=±5% power=0.25W resistance=220 package=THT]
  R3 = Resistor [tolerance=±5% power=0.25W resistance=220 package=THT]
  R4 = Resistor [tolerance=±5% power=0.25W resistance=220 package=THT]
  R5 = Resistor [tolerance=±5% power=0.25W resistance=220 package=THT]
  R6 = Resistor [tolerance=±5% power=0.25W resistance=220 package=THT]
  R7 = Resistor [tolerance=±5% power=0.25W resistance=220 package=THT]
  R8 = Resistor [tolerance=±5% power=0.25W resistance=220 package=THT]
  <100 = Pushbutton [package="[THT]"]
  100> = Pushbutton [package="[THT]"]
  Servo = Dagu DGServo 9g header (male) [package=THT]
  C1 = Ceramic Capacitor [capacitance=100nF voltage=35V package="200 mil [THT, multilayer]"]
  Analog = female pin header, 3 pins [form="♀ (female)"]
  J4 = female pin header, 3 pins [form="♀ (female)"]
  J5 = female pin header, 6 pins [form="♀ (female)"]
  J6 = female pin header, 6 pins [form="♀ (female)"]

nets:
  N1: R1.Pin_0, J1.pin1
  N2: R1.Pin_1, J5.pin6
  N3: J1.pin2, R2.Pin_0
  N4: J1.pin3, R3.Pin_0
  N5: J1.pin4, R4.Pin_0
  N6: J1.pin5, R5.Pin_0
  N7: J1.pin6, J5.pin2
  N8: J2.pin1, R8.Pin_0
  N9: J2.pin2, J6.pin2
  N10: J2.pin3, J6.pin3
  N11: J2.pin4, R7.Pin_0
  N12: J2.pin5, R6.Pin_0
  N13: J2.pin6, J6.pin6
  N14: R2.Pin_1, J5.pin5
  N15: R3.Pin_1, J5.pin4
  N16: R4.Pin_1, J5.pin3
  N17: R5.Pin_1, J5.pin1
  N18: R6.Pin_1, J6.pin5
  N19: R7.Pin_1, J6.pin4
  N20: R8.Pin_1, J6.pin1
  N21: <100.Pin_1, <100.Pin_2, Analog.pin2
  N22: <100.Pin_3, <100.Pin_4, 100>.Pin_3, 100>.Pin_4, Servo.gnd, C1.1, J4.pin2, J4.pin3
  N23: 100>.Pin_1, 100>.Pin_2, Analog.pin3
  N24: Servo.Vcc, C1.0, J4.pin1
  N25: Servo.pulse, Analog.pin1

notes:
  E D * C G 4
  1 A F 2 3 B
  PPM
  VCC
  GND
  B
  D3
  D2
  F
  A
  D1
  G
  D4
  C
  *
  D
  E
  5V
  A3
  A4
  A5
